// Logisim project root.circ as structural Verilog
module main (
);

  wire button_1_out, button_2_out, clk, controlpath_1_load, controlpath_1_store;
  wire [7:0] adder_1_out, controlpath_1_sign, datapath_1_address, datapath_1_dataout, ram_1_dout,
       register_1_q;
  wire [23:0] rom_1_data;

  Clock clock_1 (.out(clk));
  Register register_1 (.D(adder_1_out), .Q(register_1_q), .clk(clk), .clr(button_1_out));  // open: en
  Button button_1 (.out(button_1_out));
  Adder adder_1 (.a(register_1_q), .b(8'h1), .out(adder_1_out));  // open: cin, cout
  ROM #(.dataWidth(24)) rom_1 (.addr(register_1_q), .data(rom_1_data));
  DataPath datapath_1 (
    .Sign(controlpath_1_sign), .DataIn(ram_1_dout), .Params(rom_1_data[15:0]), .clk(clk),
    .Address(datapath_1_address), .DataOut(datapath_1_dataout));
  ControlPath controlpath_1 (
    .Opcode(rom_1_data[23:16]), .Load(controlpath_1_load), .Store(controlpath_1_store),
    .Sign(controlpath_1_sign));
  RAM #(.clearpin("true"), .\type ("nonvolatile")) ram_1 (
    .addr(datapath_1_address), .we(controlpath_1_store), .oe(controlpath_1_load), .clk(clk),
    .din(datapath_1_dataout), .dout(ram_1_dout), .clr(button_2_out));
  Button button_2 (.out(button_2_out));

  // Notes on the sheet:
  //   contents of rom_1 (hex, n*v repeats v):
  //   5000a 70000 50003 70100 60000 80001 70200
endmodule

module ControlPath (
  input  [7:0] Opcode,
  output Load,
  output Store,
  output [7:0] Sign
);

  wire and_1_out, and_4_out, and_5_out, not_1_out, not_2_out, not_4_out;

  not not_1 (not_1_out, Opcode[6]);
  not not_2 (not_2_out, Opcode[2]);
  not not_3 (Sign[2], Opcode[1]);
  not not_4 (not_4_out, Opcode[0]);
  and and_1 (and_1_out, not_1_out, not_4_out);
  and and_2 (Store, Opcode[1], Opcode[0]);
  and and_3 (Sign[3], Opcode[1], Opcode[0]);
  and and_4 (and_4_out, Opcode[1], Opcode[0]);
  and and_5 (and_5_out, not_2_out, Opcode[1]);
  or or_1 (Load, Sign[2], and_1_out);
  or or_2 (Sign[0], and_4_out, and_5_out);

  assign {Sign[7:4], Sign[1]} = 5'b00001;
endmodule

module DataPath (
  input  [7:0] Sign,
  input  [7:0] DataIn,
  input  [15:0] Params,
  input  clk,
  output [7:0] Address,
  output [7:0] DataOut
);

  wire decoder_1_out0, decoder_1_out1;
  wire [4:0] multiplexer_5_out;
  wire [7:0] multiplexer_1_out, multiplexer_2_out, multiplexer_4_out, regA_q, regB_q, regOut;

  Multiplexer #(.width(8)) multiplexer_1 (.in0(DataIn), .in1(Params[7:0]), .out(multiplexer_1_out), .sel(Sign[2]));
  Multiplexer #(.width(8)) multiplexer_2 (.in0(DataIn), .in1(Params[7:0]), .out(multiplexer_2_out), .sel(Sign[1]));
  ULA ula_1 ();
  Multiplexer #(.width(8)) multiplexer_3 (.in0(multiplexer_2_out), .in1(regOut), .out(DataOut), .sel(Sign[0]));
  Multiplexer #(.width(8)) multiplexer_4 (
    .in0(multiplexer_1_out), .in1(regOut), .out(multiplexer_4_out), .sel(Sign[0]));
  Multiplexer #(.width(5)) multiplexer_5 (.in0(Params[12:8]), .in1({5{1'b1}}), .out(multiplexer_5_out), .sel(Sign[3]));
  Decoder #(.enable("false"), .select(5)) decoder_1 (
    .out0(decoder_1_out0), .out1(decoder_1_out1), .sel(multiplexer_5_out));  // open: out2, out3, out4, out5, out6, out7, out8, out9, out10, out11, out12, out13, out14, out15, out16, out17, out18, out19, out20, out21, out22, out23, out24, out25, out26, out27, out28, out29, out30, out31
  Register regA (.D(multiplexer_4_out), .en(decoder_1_out0), .Q(regA_q), .clk(clk));  // open: clr
  Register regB (.D(multiplexer_4_out), .en(decoder_1_out1), .Q(regB_q), .clk(clk));  // open: clr
  Multiplexer #(.select(5), .width(8)) multiplexer_6 (
    .in0(regA_q), .in1(regB_q), .out(regOut), .sel(Params[4:0]));  // open: in2, in3, in4, in5, in6, in7, in8, in9, in10, in11, in12, in13, in14, in15, in16, in17, in18, in19, in20, in21, in22, in23, in24, in25, in26, in27, in28, in29, in30, in31

  assign Address = Params[15:8];

  // Other names for the same wires on the sheet: param2[7:0] = Params[7:0]; param1[7:0] = Params[15:8];
  //   selDataOut0 = Sign[0]; selDataIn1 = Sign[1]
endmodule
